// Logisim project sqrt2.circ as structural Verilog: 32 circuits, main circuit main
module main (
  input  ENABLE,
  input  [15:0] IO_DATA_IN,
  output NAN,
  output PINF,
  output NINF,
  output RESULT,
  output [15:0] IO_DATA_OUT
);

  wire CLK_out;

  Clock CLK (.out(CLK_out));
  sqrt sqrt_1 (
    .CLK(CLK_out), .ENABLE(ENABLE), .IO_DATA_IN(IO_DATA_IN), .IS_NAN(NAN), .IS_NINF(PINF), .IS_PINF(NINF),
    .RESULT(RESULT), .IO_DATA_OUT(IO_DATA_OUT));
endmodule

module sqrt (
  input  CLK,
  input  ENABLE,
  input  [15:0] IO_DATA_IN,
  output IS_NAN,
  output IS_NINF,
  output IS_PINF,
  output RESULT,
  output [15:0] IO_DATA_OUT
);

  wire and_1_out, and_2_out, and_4_out, and_5_out, and_7_out, clkfirstdata_1_sign, comparator22_1_aisgreater,
       NE, not_2_out, not_3_out, NotS, RCLK, RCLK2, special_1_denorm, T;
  wire [4:0] clkfirstdata_1_exp, denormexpcolculation_1_exp, expcolculation_1_exp, multiplexor5_1_ans,
       mycounter_1_ans;
  wire [9:0] clkfirstdata_1_mant, multiplexor10_1_ans;
  wire [10:0] normalization_1_mant11;
  wire [15:0] firstdata_1_mant, multiplexor16_1_ans, SData;
  wire [21:0] clkdata_1_dataout, clkdata_2_dataout, clkdata_3_dataout, denormexpcolculation_1_mant22,
       expcolculation_1_mant22, multiplexor22_1_ans, multiplexor22_2_ans, multiplexor22_3_ans,
       multiplexor22_4_ans, normalization_1_numberofshifts, oneiteration_1_ansout,
       oneiteration_1_iterationout, oneiteration_1_mantout;

  not not_1 (NE, ENABLE);
  MyCounter mycounter_1 (.C(CLK), .Reset(NE), .ans(mycounter_1_ans));
  Comparator22 comparator22_1 (.A({{17{1'b0}}, mycounter_1_ans}), .B(22'hc), .AIsGreater(comparator22_1_aisgreater));
  and and_1 (and_1_out, ~T, ~and_4_out, ~NotS);  // AND_Gate
  and and_2 (and_2_out, CLK, ~and_4_out, ~comparator22_1_aisgreater);  // AND_Gate
  and and_3 (T, ~mycounter_1_ans[0], ~mycounter_1_ans[1], ~mycounter_1_ans[2], ~mycounter_1_ans[3], ~mycounter_1_ans[4]);  // AND_Gate
  and and_4 (and_4_out, mycounter_1_ans[0], ~mycounter_1_ans[1], ~mycounter_1_ans[2], ~mycounter_1_ans[3], ~mycounter_1_ans[4]);  // AND_Gate
  not not_2 (not_2_out, and_2_out);
  or or_1 (RESULT, comparator22_1_aisgreater, and_1_out);
  and and_5 (and_5_out, and_4_out, ~CLK);  // AND_Gate
  not not_3 (not_3_out, not_2_out);
  xor xor_1 (RCLK, and_2_out, not_3_out);
  and and_6 (RCLK2, RCLK, CLK);
  FirstData firstdata_1 (.enable(and_4_out), .DataIn(IO_DATA_IN), .mant(firstdata_1_mant));
  CLKFirstData clkfirstdata_1 (
    .C(and_5_out), .DataIn(firstdata_1_mant), .Reset(NE), .mant(clkfirstdata_1_mant),
    .exp(clkfirstdata_1_exp), .Sign(clkfirstdata_1_sign));
  and and_7 (and_7_out, ~T, ~and_4_out, ~NE);  // AND_Gate
  FirstData firstdata_2 (.enable(and_7_out), .DataIn(multiplexor16_1_ans), .mant(IO_DATA_IN));
  Multiplexor10 multiplexor10_1 (.A(clkfirstdata_1_mant), .IsA(NotS), .B({10{1'b0}}), .ans(multiplexor10_1_ans));
  Special special_1 (
    .mant(clkfirstdata_1_mant), .exp(clkfirstdata_1_exp), .sign(clkfirstdata_1_sign),
    .Denorm(special_1_denorm), .NotSpicial(NotS), .Nan(IS_NAN), .NInf(IS_NINF), .PInf(IS_PINF),
    .SpicialData(SData));  // open: Norm
  Normalization normalization_1 (
    .mant(multiplexor10_1_ans), .mant11(normalization_1_mant11),
    .NumberOfShifts(normalization_1_numberofshifts));
  ExpColculation expcolculation_1 (
    .MantIn(multiplexor10_1_ans), .Denorm(1'b0), .ExpIn(clkfirstdata_1_exp),
    .mant22(expcolculation_1_mant22), .exp(expcolculation_1_exp));
  DenormExpColculation denormexpcolculation_1 (
    .mant(normalization_1_mant11), .NumberOfShifts(normalization_1_numberofshifts),
    .mant22(denormexpcolculation_1_mant22), .exp(denormexpcolculation_1_exp));
  Multiplexor22 multiplexor22_1 (
    .A(denormexpcolculation_1_mant22), .IsA(special_1_denorm), .B(expcolculation_1_mant22),
    .ans(multiplexor22_1_ans));
  Multiplexor5 multiplexor5_1 (
    .A(denormexpcolculation_1_exp), .IsA(special_1_denorm), .B(expcolculation_1_exp), .ans(multiplexor5_1_ans));
  Multiplexor22 multiplexor22_2 (
    .A(multiplexor22_1_ans), .IsA(and_4_out), .B(clkdata_1_dataout), .ans(multiplexor22_2_ans));
  Multiplexor22 multiplexor22_3 (.A({22{1'b0}}), .IsA(and_4_out), .B(clkdata_2_dataout), .ans(multiplexor22_3_ans));
  Multiplexor22 multiplexor22_4 (.A(22'hb), .IsA(and_4_out), .B(clkdata_3_dataout), .ans(multiplexor22_4_ans));
  OneIteration oneiteration_1 (
    .mantIn(multiplexor22_2_ans), .ansIn(multiplexor22_3_ans), .iterationIn(multiplexor22_4_ans), .C(RCLK2),
    .reset(NE), .mantOut(oneiteration_1_mantout), .ansOut(oneiteration_1_ansout),
    .iterationOut(oneiteration_1_iterationout));
  CLKData clkdata_1 (.C(RCLK), .Reset(NE), .DataIn(oneiteration_1_mantout), .Dataout(clkdata_1_dataout));
  CLKData clkdata_2 (.C(RCLK), .Reset(NE), .DataIn(oneiteration_1_ansout), .Dataout(clkdata_2_dataout));
  CLKData clkdata_3 (.C(RCLK), .Reset(NE), .DataIn(oneiteration_1_iterationout), .Dataout(clkdata_3_dataout));
  Multiplexor16 multiplexor16_1 (
    .A({1'b0, multiplexor5_1_ans, oneiteration_1_ansout[9:0]}), .IsA(NotS), .B(SData),
    .ans(multiplexor16_1_ans));

  assign IO_DATA_OUT = IO_DATA_IN;

  // Other names for the same wires on the sheet: C = CLK
endmodule

module Dtrigger (
  input  D,
  input  C,
  input  Reset,
  output Q,
  output NQ
);

  wire nand_1_out, nand_2_out, nand_4_out, or_1_out, por_1_out;

  POR por_1 (.out(por_1_out));
  nand nand_1 (nand_1_out, D, C);
  nand nand_2 (nand_2_out, nand_1_out, C);
  or or_1 (or_1_out, Reset, por_1_out);
  nand nand_3 (Q, nand_1_out, NQ);
  nand nand_4 (nand_4_out, Q, nand_2_out);
  or or_2 (NQ, nand_4_out, or_1_out);
endmodule

module Special (
  input  [9:0] mant,
  input  [4:0] exp,
  input  sign,
  output Norm,
  output Denorm,
  output NotSpicial,
  output Nan,
  output NInf,
  output PInf,
  output [15:0] SpicialData
);

  wire and_1_out, and_2_out, and_3_out, and_4_out, and_6_out, and_7_out, Zero;
  wire [15:0] multiplexor16_1_ans, multiplexor16_2_ans;

  and and_1 (and_1_out, ~exp[0], ~exp[1], ~exp[2], ~exp[3], ~exp[4]);  // AND_Gate
  and and_2 (and_2_out, ~mant[0], ~mant[1], ~mant[2], ~mant[3], ~mant[4], ~mant[5], ~mant[6], ~mant[7], ~mant[8], ~mant[9]);  // AND_Gate
  and and_3 (and_3_out, exp[0], exp[1], exp[2], exp[3], exp[4]);
  and and_4 (and_4_out, ~exp[0], ~exp[1], ~exp[2], ~exp[3], ~exp[4]);  // AND_Gate
  and and_5 (Zero, and_2_out, and_4_out);
  and and_6 (and_6_out, ~Zero, sign);  // AND_Gate
  and and_7 (and_7_out, ~and_2_out, and_3_out);  // AND_Gate
  and and_8 (PInf, and_2_out, and_3_out, ~sign);  // AND_Gate
  or or_1 (Nan, and_7_out, and_6_out);
  Multiplexor16 multiplexor16_1 (
    .A({sign, {6{1'b1}}, mant[8:0]}), .IsA(and_7_out), .B({sign, exp, mant}), .ans(multiplexor16_1_ans));
  and and_9 (NotSpicial, ~Nan, ~Zero, ~PInf);  // AND_Gate
  and and_10 (Norm, ~and_1_out, NotSpicial);  // AND_Gate
  and and_11 (Denorm, and_1_out, NotSpicial);
  Multiplexor16 multiplexor16_2 (.A(16'hfe00), .IsA(and_6_out), .B(multiplexor16_1_ans), .ans(multiplexor16_2_ans));
  Multiplexor16 multiplexor16_3 (.A({sign, {15{1'b0}}}), .IsA(Zero), .B(multiplexor16_2_ans), .ans(SpicialData));

  assign NInf = 1'b0;
endmodule

module ExpColculation (
  input  [9:0] MantIn,
  input  Denorm,
  input  [4:0] ExpIn,
  output [21:0] mant22,
  output [4:0] exp
);

  wire not_2_out;
  wire [10:10] not_1_out;
  wire [21:0] shift1_1_ans, summator22_1_sum, summator22_2_sum;
  wire [21:5] multiplexor22_1_ans;

  not not_1 (not_1_out[10], Denorm);
  not not_2 (not_2_out, ExpIn[0]);
  Summator22 summator22_1 (.A({{18{1'b0}}, ExpIn[4:1]}), .B(22'h7), .C(1'b0), .Sum(summator22_1_sum));  // open: Cout
  Summator22 summator22_2 (.A({{18{1'b0}}, ExpIn[4:1]}), .B(22'h8), .C(1'b0), .Sum(summator22_2_sum));  // open: Cout
  Shift1 shift1_1 (.A({1'b0, not_1_out[10], MantIn, {10{1'b0}}}), .ans(shift1_1_ans));
  Multiplexor22 multiplexor22_1 (
    .A(summator22_1_sum), .IsA(not_2_out), .B(summator22_2_sum), .ans({multiplexor22_1_ans, exp}));
  Multiplexor22 multiplexor22_2 (
    .A(shift1_1_ans), .IsA(not_2_out), .B({1'b0, not_1_out[10], MantIn, {10{1'b0}}}), .ans(mant22));
endmodule

module Summator1 (
  input  A,
  input  B,
  input  C,
  output Sum,
  output Cout
);

  wire and_1_out, and_2_out, xor_1_out;

  xor xor_1 (xor_1_out, A, B);
  xor xor_2 (Sum, xor_1_out, C);
  and and_1 (and_1_out, xor_1_out, C);
  and and_2 (and_2_out, A, B);
  or or_1 (Cout, and_1_out, and_2_out);
endmodule

module Summator4 (
  input  [3:0] A,
  input  [3:0] B,
  input  C,
  output Cout,
  output [3:0] Sum
);

  wire summator1_1_cout, summator1_2_cout, summator1_3_cout;

  Summator1 summator1_1 (.A(A[0]), .B(B[0]), .C(C), .Sum(Sum[0]), .Cout(summator1_1_cout));
  Summator1 summator1_2 (.A(A[1]), .B(B[1]), .C(summator1_1_cout), .Sum(Sum[1]), .Cout(summator1_2_cout));
  Summator1 summator1_3 (.A(A[2]), .B(B[2]), .C(summator1_2_cout), .Sum(Sum[2]), .Cout(summator1_3_cout));
  Summator1 summator1_4 (.A(A[3]), .B(B[3]), .C(summator1_3_cout), .Sum(Sum[3]), .Cout(Cout));
endmodule

module Summator22 (
  input  [21:0] A,
  input  [21:0] B,
  input  C,
  output Cout,
  output [21:0] Sum
);

  wire summator4_1_cout, summator4_2_cout, summator4_3_cout, summator4_4_cout, summator4_5_cout;

  Summator4 summator4_1 (.A(A[3:0]), .B(B[3:0]), .C(C), .Cout(summator4_1_cout), .Sum(Sum[3:0]));
  Summator4 summator4_2 (.A(A[7:4]), .B(B[7:4]), .C(summator4_1_cout), .Cout(summator4_2_cout), .Sum(Sum[7:4]));
  Summator4 summator4_3 (.A(A[11:8]), .B(B[11:8]), .C(summator4_2_cout), .Cout(summator4_3_cout), .Sum(Sum[11:8]));
  Summator4 summator4_4 (.A(A[15:12]), .B(B[15:12]), .C(summator4_3_cout), .Cout(summator4_4_cout), .Sum(Sum[15:12]));
  Summator4 summator4_5 (.A(A[19:16]), .B(B[19:16]), .C(summator4_4_cout), .Cout(summator4_5_cout), .Sum(Sum[19:16]));
  Summator2 summator2_1 (.A(A[21:20]), .B(B[21:20]), .C(summator4_5_cout), .Cout(Cout), .Sum(Sum[21:20]));
endmodule

module Substractor22 (
  input  [21:0] A,
  input  [21:0] B,
  output IsPositive,
  output [21:0] ans
);

  wire [21:0] not_1_out, summator22_1_sum;

  assign not_1_out = ~B;  // NOT_Gate not_1, 22 bits wide
  Summator22 summator22_1 (.A(not_1_out), .B(22'h1), .C(1'b0), .Sum(summator22_1_sum));  // open: Cout
  Summator22 summator22_2 (.A(A), .B(summator22_1_sum), .C(1'b0), .Cout(IsPositive), .Sum(ans));
endmodule

module Comparator22 (
  input  [21:0] A,
  input  [21:0] B,
  output AIsGreater
);

  Substractor22 substractor22_1 (.A(A), .B(B), .IsPositive(AIsGreater));  // open: ans
endmodule

module Shift1 (
  input  [21:0] A,
  output [21:0] ans
);


  assign ans = {A[20:0], 1'b0};
endmodule

module Shift2 (
  input  [21:0] A,
  output [21:0] ans
);

  wire [21:0] shift1_1_ans;

  Shift1 shift1_1 (.A(A), .ans(shift1_1_ans));
  Shift1 shift1_2 (.A(shift1_1_ans), .ans(ans));
endmodule

module Shift4 (
  input  [21:0] A,
  output [21:0] ans
);

  wire [21:0] shift2_1_ans;

  Shift2 shift2_1 (.A(A), .ans(shift2_1_ans));
  Shift2 shift2_2 (.A(shift2_1_ans), .ans(ans));
endmodule

module Shift8 (
  input  [21:0] A,
  output [21:0] ans
);

  wire [21:0] shift4_1_ans;

  Shift4 shift4_1 (.A(A), .ans(shift4_1_ans));
  Shift4 shift4_2 (.A(shift4_1_ans), .ans(ans));
endmodule

module Shift16 (
  input  [21:0] A,
  output [21:0] ans
);

  wire [21:0] shift8_1_ans;

  Shift8 shift8_1 (.A(A), .ans(shift8_1_ans));
  Shift8 shift8_2 (.A(shift8_1_ans), .ans(ans));
endmodule

module Multiplexor22 (
  input  [21:0] A,
  input  IsA,
  input  [21:0] B,
  output [21:0] ans
);

  wire [21:0] and_1_out, and_2_out;

  assign and_1_out = A & {22{IsA}};  // AND_Gate and_1, 22 bits wide
  assign and_2_out = ~{22{IsA}} & B;  // AND_Gate and_2, 22 bits wide
  assign ans = and_1_out | and_2_out;  // OR_Gate or_1, 22 bits wide
endmodule

module Shift2x (
  input  [21:0] A,
  input  [21:0] X,
  output [21:0] ans
);

  wire [21:0] multiplexor22_1_ans, multiplexor22_2_ans, multiplexor22_3_ans, shift1_1_ans, shift2_1_ans,
       shift4_1_ans, shift8_1_ans, shift16_1_ans;

  Shift1 shift1_1 (.A(X), .ans(shift1_1_ans));
  Shift2 shift2_1 (.A(A), .ans(shift2_1_ans));
  Multiplexor22 multiplexor22_1 (.A(shift2_1_ans), .IsA(shift1_1_ans[1]), .B(A), .ans(multiplexor22_1_ans));
  Shift4 shift4_1 (.A(multiplexor22_1_ans), .ans(shift4_1_ans));
  Multiplexor22 multiplexor22_2 (
    .A(shift4_1_ans), .IsA(shift1_1_ans[2]), .B(multiplexor22_1_ans), .ans(multiplexor22_2_ans));
  Shift8 shift8_1 (.A(multiplexor22_2_ans), .ans(shift8_1_ans));
  Multiplexor22 multiplexor22_3 (
    .A(shift8_1_ans), .IsA(shift1_1_ans[3]), .B(multiplexor22_2_ans), .ans(multiplexor22_3_ans));
  Shift16 shift16_1 (.A(multiplexor22_3_ans), .ans(shift16_1_ans));
  Multiplexor22 multiplexor22_4 (.A(shift16_1_ans), .IsA(shift1_1_ans[4]), .B(multiplexor22_3_ans), .ans(ans));
endmodule

module Summator2 (
  input  [1:0] A,
  input  [1:0] B,
  input  C,
  output Cout,
  output [1:0] Sum
);

  wire summator1_1_cout;

  Summator1 summator1_1 (.A(A[0]), .B(B[0]), .C(C), .Sum(Sum[0]), .Cout(summator1_1_cout));
  Summator1 summator1_2 (.A(A[1]), .B(B[1]), .C(summator1_1_cout), .Sum(Sum[1]), .Cout(Cout));
endmodule

module Normalization (
  input  [9:0] mant,
  output [10:0] mant11,
  output [21:0] NumberOfShifts
);

  wire not_1_out, not_2_out, not_3_out, not_4_out, not_5_out, not_6_out, not_7_out, not_8_out, not_9_out,
       not_10_out;
  wire [10:0] multiplexor11_1_ans, multiplexor11_2_ans, multiplexor11_3_ans, multiplexor11_4_ans,
       multiplexor11_5_ans, multiplexor11_6_ans, multiplexor11_7_ans, multiplexor11_8_ans,
       multiplexor11_9_ans, shiftfor11_1_ans, shiftfor11_2_ans, shiftfor11_3_ans, shiftfor11_4_ans,
       shiftfor11_5_ans, shiftfor11_6_ans, shiftfor11_7_ans, shiftfor11_8_ans, shiftfor11_9_ans,
       shiftfor11_10_ans;
  wire [21:0] multiplexor22_1_ans, multiplexor22_2_ans, multiplexor22_3_ans, multiplexor22_4_ans,
       multiplexor22_5_ans, multiplexor22_6_ans, multiplexor22_7_ans, multiplexor22_8_ans,
       multiplexor22_9_ans, summator22_1_sum, summator22_2_sum, summator22_3_sum, summator22_4_sum,
       summator22_5_sum, summator22_6_sum, summator22_7_sum, summator22_8_sum, summator22_9_sum;

  ShiftFor11 shiftfor11_1 (.A({1'b0, mant}), .ans(shiftfor11_1_ans));
  not not_1 (not_1_out, 1'b0);
  Multiplexor11 multiplexor11_1 (.A(shiftfor11_1_ans), .IsA(not_1_out), .B({1'b0, mant}), .ans(multiplexor11_1_ans));
  Multiplexor22 multiplexor22_1 (.A(22'h1), .IsA(not_1_out), .B({22{1'b0}}), .ans(multiplexor22_1_ans));
  Summator22 summator22_1 (.A(multiplexor22_1_ans), .B(22'h1), .Sum(summator22_1_sum));  // open: C, Cout
  ShiftFor11 shiftfor11_2 (.A(multiplexor11_1_ans), .ans(shiftfor11_2_ans));
  not not_2 (not_2_out, multiplexor11_1_ans[10]);
  Multiplexor11 multiplexor11_2 (
    .A(shiftfor11_2_ans), .IsA(not_2_out), .B(multiplexor11_1_ans), .ans(multiplexor11_2_ans));
  Multiplexor22 multiplexor22_2 (
    .A(summator22_1_sum), .IsA(not_2_out), .B(multiplexor22_1_ans), .ans(multiplexor22_2_ans));
  Summator22 summator22_2 (.A(multiplexor22_2_ans), .B(22'h1), .Sum(summator22_2_sum));  // open: C, Cout
  ShiftFor11 shiftfor11_3 (.A(multiplexor11_2_ans), .ans(shiftfor11_3_ans));
  not not_3 (not_3_out, multiplexor11_2_ans[10]);
  Multiplexor11 multiplexor11_3 (
    .A(shiftfor11_3_ans), .IsA(not_3_out), .B(multiplexor11_2_ans), .ans(multiplexor11_3_ans));
  Multiplexor22 multiplexor22_3 (
    .A(summator22_2_sum), .IsA(not_3_out), .B(multiplexor22_2_ans), .ans(multiplexor22_3_ans));
  Summator22 summator22_3 (.A(multiplexor22_3_ans), .B(22'h1), .Sum(summator22_3_sum));  // open: C, Cout
  ShiftFor11 shiftfor11_4 (.A(multiplexor11_3_ans), .ans(shiftfor11_4_ans));
  not not_4 (not_4_out, multiplexor11_3_ans[10]);
  Multiplexor11 multiplexor11_4 (
    .A(shiftfor11_4_ans), .IsA(not_4_out), .B(multiplexor11_3_ans), .ans(multiplexor11_4_ans));
  Multiplexor22 multiplexor22_4 (
    .A(summator22_3_sum), .IsA(not_4_out), .B(multiplexor22_3_ans), .ans(multiplexor22_4_ans));
  Summator22 summator22_4 (.A(multiplexor22_4_ans), .B(22'h1), .Sum(summator22_4_sum));  // open: C, Cout
  ShiftFor11 shiftfor11_5 (.A(multiplexor11_4_ans), .ans(shiftfor11_5_ans));
  not not_5 (not_5_out, multiplexor11_4_ans[10]);
  Multiplexor11 multiplexor11_5 (
    .A(shiftfor11_5_ans), .IsA(not_5_out), .B(multiplexor11_4_ans), .ans(multiplexor11_5_ans));
  Multiplexor22 multiplexor22_5 (
    .A(summator22_4_sum), .IsA(not_5_out), .B(multiplexor22_4_ans), .ans(multiplexor22_5_ans));
  Summator22 summator22_5 (.A(multiplexor22_5_ans), .B(22'h1), .Sum(summator22_5_sum));  // open: C, Cout
  ShiftFor11 shiftfor11_6 (.A(multiplexor11_5_ans), .ans(shiftfor11_6_ans));
  not not_6 (not_6_out, multiplexor11_5_ans[10]);
  Multiplexor11 multiplexor11_6 (
    .A(shiftfor11_6_ans), .IsA(not_6_out), .B(multiplexor11_5_ans), .ans(multiplexor11_6_ans));
  Multiplexor22 multiplexor22_6 (
    .A(summator22_5_sum), .IsA(not_6_out), .B(multiplexor22_5_ans), .ans(multiplexor22_6_ans));
  Summator22 summator22_6 (.A(multiplexor22_6_ans), .B(22'h1), .Sum(summator22_6_sum));  // open: C, Cout
  ShiftFor11 shiftfor11_7 (.A(multiplexor11_6_ans), .ans(shiftfor11_7_ans));
  not not_7 (not_7_out, multiplexor11_6_ans[10]);
  Multiplexor11 multiplexor11_7 (
    .A(shiftfor11_7_ans), .IsA(not_7_out), .B(multiplexor11_6_ans), .ans(multiplexor11_7_ans));
  Multiplexor22 multiplexor22_7 (
    .A(summator22_6_sum), .IsA(not_7_out), .B(multiplexor22_6_ans), .ans(multiplexor22_7_ans));
  Summator22 summator22_7 (.A(multiplexor22_7_ans), .B(22'h1), .Sum(summator22_7_sum));  // open: C, Cout
  ShiftFor11 shiftfor11_8 (.A(multiplexor11_7_ans), .ans(shiftfor11_8_ans));
  not not_8 (not_8_out, multiplexor11_7_ans[10]);
  Multiplexor11 multiplexor11_8 (
    .A(shiftfor11_8_ans), .IsA(not_8_out), .B(multiplexor11_7_ans), .ans(multiplexor11_8_ans));
  Multiplexor22 multiplexor22_8 (
    .A(summator22_7_sum), .IsA(not_8_out), .B(multiplexor22_7_ans), .ans(multiplexor22_8_ans));
  Summator22 summator22_8 (.A(multiplexor22_8_ans), .B(22'h1), .Sum(summator22_8_sum));  // open: C, Cout
  ShiftFor11 shiftfor11_9 (.A(multiplexor11_8_ans), .ans(shiftfor11_9_ans));
  not not_9 (not_9_out, multiplexor11_8_ans[10]);
  Multiplexor11 multiplexor11_9 (
    .A(shiftfor11_9_ans), .IsA(not_9_out), .B(multiplexor11_8_ans), .ans(multiplexor11_9_ans));
  Multiplexor22 multiplexor22_9 (
    .A(summator22_8_sum), .IsA(not_9_out), .B(multiplexor22_8_ans), .ans(multiplexor22_9_ans));
  Summator22 summator22_9 (.A(multiplexor22_9_ans), .B(22'h1), .Sum(summator22_9_sum));  // open: C, Cout
  ShiftFor11 shiftfor11_10 (.A(multiplexor11_9_ans), .ans(shiftfor11_10_ans));
  not not_10 (not_10_out, multiplexor11_9_ans[10]);
  Multiplexor11 multiplexor11_10 (.A(shiftfor11_10_ans), .IsA(not_10_out), .B(multiplexor11_9_ans), .ans(mant11));
  Multiplexor22 multiplexor22_10 (
    .A(summator22_9_sum), .IsA(not_10_out), .B(multiplexor22_9_ans), .ans(NumberOfShifts));
endmodule

module Multiplexor5 (
  input  [4:0] A,
  input  IsA,
  input  [4:0] B,
  output [4:0] ans
);

  wire [4:0] and_1_out, and_2_out;

  assign and_1_out = A & {5{IsA}};  // AND_Gate and_1, 5 bits wide
  assign and_2_out = ~{5{IsA}} & B;  // AND_Gate and_2, 5 bits wide
  assign ans = and_1_out | and_2_out;  // OR_Gate or_1, 5 bits wide
endmodule

module CLKDtrigger (
  input  D,
  input  C,
  input  Reset,
  output NQ,
  output Q
);

  wire nand_1_out, nand_2_out, nand_3_out, nand_4_out, nor_1_out, por_1_out;

  POR por_1 (.out(por_1_out));
  nand nand_1 (nand_1_out, D, nor_1_out, nand_2_out);
  nand nand_2 (nand_2_out, nand_1_out, C, nand_3_out);
  nand nand_3 (nand_3_out, C, nor_1_out, nand_4_out);
  nand nand_4 (nand_4_out, nand_3_out, nand_1_out);
  nor nor_1 (nor_1_out, Reset, por_1_out);
  nand nand_5 (NQ, nor_1_out, nand_2_out, Q);
  nand nand_6 (Q, NQ, nand_3_out);
endmodule

module MyCounter (
  input  C,
  input  Reset,
  output [4:0] ans
);

  wire and_1_out, and_2_out, and_3_out, clkdtrigger_1_nq, xor_1_out, xor_2_out, xor_3_out, xor_4_out;

  xor xor_1 (xor_1_out, ans[1], ans[0]);
  xor xor_2 (xor_2_out, ans[2], and_1_out);
  xor xor_3 (xor_3_out, ans[4], and_3_out);
  xor xor_4 (xor_4_out, ans[3], and_2_out);
  CLKDtrigger clkdtrigger_1 (.D(clkdtrigger_1_nq), .C(C), .Reset(Reset), .NQ(clkdtrigger_1_nq), .Q(ans[0]));
  CLKDtrigger clkdtrigger_2 (.D(xor_1_out), .C(C), .Reset(Reset), .Q(ans[1]));  // open: NQ
  CLKDtrigger clkdtrigger_3 (.D(xor_2_out), .C(C), .Reset(Reset), .Q(ans[2]));  // open: NQ
  CLKDtrigger clkdtrigger_4 (.D(xor_4_out), .C(C), .Reset(Reset), .Q(ans[3]));  // open: NQ
  CLKDtrigger clkdtrigger_5 (.D(xor_3_out), .C(C), .Reset(Reset), .Q(ans[4]));  // open: NQ
  and and_1 (and_1_out, ans[0], ans[1]);
  and and_2 (and_2_out, and_1_out, ans[2]);
  and and_3 (and_3_out, and_2_out, ans[3]);

  // Other names for the same wires on the sheet: R = Reset
endmodule

module Multiplexor11 (
  input  [10:0] A,
  input  IsA,
  input  [10:0] B,
  output [10:0] ans
);

  wire [10:0] and_1_out, and_2_out;

  assign and_1_out = A & {11{IsA}};  // AND_Gate and_1, 11 bits wide
  assign and_2_out = ~{11{IsA}} & B;  // AND_Gate and_2, 11 bits wide
  assign ans = and_1_out | and_2_out;  // OR_Gate or_1, 11 bits wide
endmodule

module ShiftFor11 (
  input  [10:0] A,
  output [10:0] ans
);


  assign ans = {A[9:0], 1'b0};
endmodule

module DenormExpColculation (
  input  [10:0] mant,
  input  [21:0] NumberOfShifts,
  output [21:0] mant22,
  output [4:0] exp
);

  wire [21:0] shift1_1_ans, substractor22_1_ans, substractor22_2_ans;
  wire [21:5] multiplexor22_1_ans;

  Substractor22 substractor22_1 (
    .A(22'h7), .B({1'b0, NumberOfShifts[21:1]}), .ans(substractor22_1_ans));  // open: IsPositive
  Substractor22 substractor22_2 (
    .A(22'h8), .B({1'b0, NumberOfShifts[21:1]}), .ans(substractor22_2_ans));  // open: IsPositive
  Shift1 shift1_1 (.A({1'b0, mant, {10{1'b0}}}), .ans(shift1_1_ans));
  Multiplexor22 multiplexor22_1 (
    .A(substractor22_1_ans), .IsA(NumberOfShifts[0]), .B(substractor22_2_ans),
    .ans({multiplexor22_1_ans, exp}));
  Multiplexor22 multiplexor22_2 (.A(shift1_1_ans), .IsA(NumberOfShifts[0]), .B({1'b0, mant, {10{1'b0}}}), .ans(mant22));
endmodule

module OneIteration (
  input  [21:0] mantIn,
  input  [21:0] ansIn,
  input  [21:0] iterationIn,
  input  C,
  input  reset,
  output [21:0] mantOut,
  output [21:0] ansOut,
  output [21:0] iterationOut
);

  wire comparator22_1_aisgreater;
  wire [21:0] multiplexor22_1_ans, multiplexor22_2_ans, shift1_1_ans, shift1_2_ans, shift2x_1_ans,
       substractor22_1_ans, substractor22_2_ans, summator22_1_sum, summator22_2_sum;

  Shift1 shift1_1 (.A(ansIn), .ans(shift1_1_ans));
  Shift1 shift1_2 (.A(shift1_1_ans), .ans(shift1_2_ans));
  Substractor22 substractor22_1 (.A(iterationIn), .B(22'h1), .ans(substractor22_1_ans));  // open: IsPositive
  Summator22 summator22_1 (.A(shift1_2_ans), .B(22'h1), .C(1'b0), .Sum(summator22_1_sum));  // open: Cout
  Shift2x shift2x_1 (.A(summator22_1_sum), .X(substractor22_1_ans), .ans(shift2x_1_ans));
  Summator22 summator22_2 (.A(22'h1), .B(shift1_1_ans), .C(1'b0), .Sum(summator22_2_sum));  // open: Cout
  Comparator22 comparator22_1 (.A(mantIn), .B(shift2x_1_ans), .AIsGreater(comparator22_1_aisgreater));
  Substractor22 substractor22_2 (.A(mantIn), .B(shift2x_1_ans), .ans(substractor22_2_ans));  // open: IsPositive
  Multiplexor22 multiplexor22_1 (
    .A(substractor22_2_ans), .IsA(comparator22_1_aisgreater), .B(mantIn), .ans(multiplexor22_1_ans));
  Multiplexor22 multiplexor22_2 (
    .A(summator22_2_sum), .IsA(comparator22_1_aisgreater), .B(shift1_1_ans), .ans(multiplexor22_2_ans));
  CLKData clkdata_1 (.C(C), .Reset(reset), .DataIn(substractor22_1_ans), .Dataout(iterationOut));
  CLKData clkdata_2 (.C(C), .Reset(reset), .DataIn(multiplexor22_1_ans), .Dataout(mantOut));
  CLKData clkdata_3 (.C(C), .Reset(reset), .DataIn(multiplexor22_2_ans), .Dataout(ansOut));

  // Other names for the same wires on the sheet: R = reset
endmodule

module CLKData (
  input  C,
  input  Reset,
  input  [21:0] DataIn,
  output [21:0] Dataout
);

  CLKDtrigger clkdtrigger_1 (.D(DataIn[0]), .C(C), .Reset(Reset), .Q(Dataout[0]));  // open: NQ
  CLKDtrigger clkdtrigger_2 (.D(DataIn[1]), .C(C), .Reset(Reset), .Q(Dataout[1]));  // open: NQ
  CLKDtrigger clkdtrigger_3 (.D(DataIn[2]), .C(C), .Reset(Reset), .Q(Dataout[2]));  // open: NQ
  CLKDtrigger clkdtrigger_4 (.D(DataIn[3]), .C(C), .Reset(Reset), .Q(Dataout[3]));  // open: NQ
  CLKDtrigger clkdtrigger_5 (.D(DataIn[4]), .C(C), .Reset(Reset), .Q(Dataout[4]));  // open: NQ
  CLKDtrigger clkdtrigger_6 (.D(DataIn[5]), .C(C), .Reset(Reset), .Q(Dataout[5]));  // open: NQ
  CLKDtrigger clkdtrigger_7 (.D(DataIn[6]), .C(C), .Reset(Reset), .Q(Dataout[6]));  // open: NQ
  CLKDtrigger clkdtrigger_8 (.D(DataIn[7]), .C(C), .Reset(Reset), .Q(Dataout[7]));  // open: NQ
  CLKDtrigger clkdtrigger_9 (.D(DataIn[8]), .C(C), .Reset(Reset), .Q(Dataout[8]));  // open: NQ
  CLKDtrigger clkdtrigger_10 (.D(DataIn[9]), .C(C), .Reset(Reset), .Q(Dataout[9]));  // open: NQ
  CLKDtrigger clkdtrigger_11 (.D(DataIn[10]), .C(C), .Reset(Reset), .Q(Dataout[10]));  // open: NQ
  CLKDtrigger clkdtrigger_12 (.D(DataIn[11]), .C(C), .Reset(Reset), .Q(Dataout[11]));  // open: NQ
  CLKDtrigger clkdtrigger_13 (.D(DataIn[12]), .C(C), .Reset(Reset), .Q(Dataout[12]));  // open: NQ
  CLKDtrigger clkdtrigger_14 (.D(DataIn[13]), .C(C), .Reset(Reset), .Q(Dataout[13]));  // open: NQ
  CLKDtrigger clkdtrigger_15 (.D(DataIn[14]), .C(C), .Reset(Reset), .Q(Dataout[14]));  // open: NQ
  CLKDtrigger clkdtrigger_16 (.D(DataIn[15]), .C(C), .Reset(Reset), .Q(Dataout[15]));  // open: NQ
  CLKDtrigger clkdtrigger_17 (.D(DataIn[16]), .C(C), .Reset(Reset), .Q(Dataout[16]));  // open: NQ
  CLKDtrigger clkdtrigger_18 (.D(DataIn[17]), .C(C), .Reset(Reset), .Q(Dataout[17]));  // open: NQ
  CLKDtrigger clkdtrigger_19 (.D(DataIn[18]), .C(C), .Reset(Reset), .Q(Dataout[18]));  // open: NQ
  CLKDtrigger clkdtrigger_20 (.D(DataIn[19]), .C(C), .Reset(Reset), .Q(Dataout[19]));  // open: NQ
  CLKDtrigger clkdtrigger_21 (.D(DataIn[20]), .C(C), .Reset(Reset), .Q(Dataout[20]));  // open: NQ
  CLKDtrigger clkdtrigger_22 (.D(DataIn[21]), .C(C), .Reset(Reset), .Q(Dataout[21]));  // open: NQ

  // Other names for the same wires on the sheet: R = Reset
endmodule

module CLKFirstData (
  input  C,
  input  [15:0] DataIn,
  input  Reset,
  output [9:0] mant,
  output [4:0] exp,
  output Sign
);

  CLKDtrigger clkdtrigger_1 (.D(DataIn[0]), .C(C), .Reset(Reset), .Q(mant[0]));  // open: NQ
  CLKDtrigger clkdtrigger_2 (.D(DataIn[1]), .C(C), .Reset(Reset), .Q(mant[1]));  // open: NQ
  CLKDtrigger clkdtrigger_3 (.D(DataIn[2]), .C(C), .Reset(Reset), .Q(mant[2]));  // open: NQ
  CLKDtrigger clkdtrigger_4 (.D(DataIn[3]), .C(C), .Reset(Reset), .Q(mant[3]));  // open: NQ
  CLKDtrigger clkdtrigger_5 (.D(DataIn[4]), .C(C), .Reset(Reset), .Q(mant[4]));  // open: NQ
  CLKDtrigger clkdtrigger_6 (.D(DataIn[5]), .C(C), .Reset(Reset), .Q(mant[5]));  // open: NQ
  CLKDtrigger clkdtrigger_7 (.D(DataIn[6]), .C(C), .Reset(Reset), .Q(mant[6]));  // open: NQ
  CLKDtrigger clkdtrigger_8 (.D(DataIn[7]), .C(C), .Reset(Reset), .Q(mant[7]));  // open: NQ
  CLKDtrigger clkdtrigger_9 (.D(DataIn[8]), .C(C), .Reset(Reset), .Q(mant[8]));  // open: NQ
  CLKDtrigger clkdtrigger_10 (.D(DataIn[9]), .C(C), .Reset(Reset), .Q(mant[9]));  // open: NQ
  CLKDtrigger clkdtrigger_11 (.D(DataIn[10]), .C(C), .Reset(Reset), .Q(exp[0]));  // open: NQ
  CLKDtrigger clkdtrigger_12 (.D(DataIn[11]), .C(C), .Reset(Reset), .Q(exp[1]));  // open: NQ
  CLKDtrigger clkdtrigger_13 (.D(DataIn[12]), .C(C), .Reset(Reset), .Q(exp[2]));  // open: NQ
  CLKDtrigger clkdtrigger_14 (.D(DataIn[13]), .C(C), .Reset(Reset), .Q(exp[3]));  // open: NQ
  CLKDtrigger clkdtrigger_15 (.D(DataIn[14]), .C(C), .Reset(Reset), .Q(exp[4]));  // open: NQ
  CLKDtrigger clkdtrigger_16 (.D(DataIn[15]), .C(C), .Reset(Reset), .Q(Sign));  // open: NQ

  // Other names for the same wires on the sheet: R = Reset
endmodule

module KeyBuffer (
  input  D,
  input  key,
  output ans
);

  wire nand_1_out, nor_1_out;

  nand nand_1 (nand_1_out, D, key);
  nor nor_1 (nor_1_out, ~key, D);  // NOR_Gate
  Transistor transistor_1 (.in(1'b1), .out(ans), .gate(nand_1_out));
  Transistor #(.\type ("n")) transistor_2 (.in(1'b0), .out(ans), .gate(nor_1_out));
endmodule

module FirstData (
  input  enable,
  input  [15:0] DataIn,
  output [15:0] mant
);

  KeyBuffer keybuffer_1 (.D(DataIn[0]), .key(enable), .ans(mant[0]));
  KeyBuffer keybuffer_2 (.D(DataIn[1]), .key(enable), .ans(mant[1]));
  KeyBuffer keybuffer_3 (.D(DataIn[2]), .key(enable), .ans(mant[2]));
  KeyBuffer keybuffer_4 (.D(DataIn[3]), .key(enable), .ans(mant[3]));
  KeyBuffer keybuffer_5 (.D(DataIn[4]), .key(enable), .ans(mant[4]));
  KeyBuffer keybuffer_6 (.D(DataIn[5]), .key(enable), .ans(mant[5]));
  KeyBuffer keybuffer_7 (.D(DataIn[6]), .key(enable), .ans(mant[6]));
  KeyBuffer keybuffer_8 (.D(DataIn[7]), .key(enable), .ans(mant[7]));
  KeyBuffer keybuffer_9 (.D(DataIn[8]), .key(enable), .ans(mant[8]));
  KeyBuffer keybuffer_10 (.D(DataIn[9]), .key(enable), .ans(mant[9]));
  KeyBuffer keybuffer_11 (.D(DataIn[10]), .key(enable), .ans(mant[10]));
  KeyBuffer keybuffer_12 (.D(DataIn[11]), .key(enable), .ans(mant[11]));
  KeyBuffer keybuffer_13 (.D(DataIn[12]), .key(enable), .ans(mant[12]));
  KeyBuffer keybuffer_14 (.D(DataIn[13]), .key(enable), .ans(mant[13]));
  KeyBuffer keybuffer_15 (.D(DataIn[14]), .key(enable), .ans(mant[14]));
  KeyBuffer keybuffer_16 (.D(DataIn[15]), .key(enable), .ans(mant[15]));

  // Other names for the same wires on the sheet: E = enable
endmodule

module Multiplexor10 (
  input  [9:0] A,
  input  IsA,
  input  [9:0] B,
  output [9:0] ans
);

  wire [9:0] and_1_out, and_2_out;

  assign and_1_out = A & {10{IsA}};  // AND_Gate and_1, 10 bits wide
  assign and_2_out = ~{10{IsA}} & B;  // AND_Gate and_2, 10 bits wide
  assign ans = and_1_out | and_2_out;  // OR_Gate or_1, 10 bits wide
endmodule

module Multiplexor16 (
  input  [15:0] A,
  input  IsA,
  input  [15:0] B,
  output [15:0] ans
);

  wire [15:0] and_1_out, and_2_out;

  assign and_1_out = A & {16{IsA}};  // AND_Gate and_1, 16 bits wide
  assign and_2_out = ~{16{IsA}} & B;  // AND_Gate and_2, 16 bits wide
  assign ans = and_1_out | and_2_out;  // OR_Gate or_1, 16 bits wide
endmodule
